# Fritzing sketch batbox (saved by Fritzing 0.9.4)

parts:
  Part2 = Arduino Nano (Rev3.0)
  Part4 = Real Time Clock Module - DS1307 RTC Breakout Board
  SD_card_module1 = SD Card Module
  M1 = fc-51 [package=THT]

nets:
  GND: Part2.GND, Part4.GND, SD_card_module1.GND, M1.pin2
  N1: Part2.D4, SD_card_module1.CS
  N2: Part2.D7, M1.pin1
  N3: Part2.D11/MOSI, SD_card_module1.MOSI
  N4: Part2.D12/MISO, SD_card_module1.MISO
  5V: Part2.5V, Part4.5V, M1.pin3
  N5: Part2.A5, Part4.SCL
  N6: Part2.A4, Part4.SDA
  N7: Part2.3V3, SD_card_module1.+3.3
  N8: Part2.D13/SCK, SD_card_module1.SCK

custom parts:
  SD Card Module: SD Card Module Slot Socket Reader For Arduino ARM MCU
